# Fritzing sketch Industry_Safety_System (saved by Fritzing 0.9.3b)
breadboards: 1

parts:
  DHT1 = DHT22 Humidity and Temperature Sensor
  Part1 = MQ-4
  Part2 = Arduino Mega ADK (Rev3)

nets:
  VDD: DHT1.VDD, Part1.VCC
  N1: DHT1.DATA, Part2.D8_PWM
  GND: DHT1.GND, Part1.GND
  N2: Part1.AO, Part2.A0
